# Fritzing sketch Wiring (saved by Fritzing 1.0.5)
circuit board: 42.7251cm x 15.7796cm

parts:
  Mod1 = Raspberry Pi Pico
  Mod2 = Raspberry Pi 4B  # not connected
  Bauteil1 = Motor Driver 1A Dual TB6612FNG
  Bauteil2 = Motor Driver 1A Dual TB6612FNG
  DC_Mot_Enc1 = DC Motor with two-phase hall-encoder [part_number=VT-E-G25A-06-177E]
  BAT1 = LiPo 3S 11,1V 2200mAh 25C
  DC_Mot_Enc3 = DC Motor with two-phase hall-encoder [part_number=VT-E-G25A-06-177E]
  DC_Mot_Enc4 = DC Motor with two-phase hall-encoder [part_number=VT-E-G25A-06-177E]
  DC_Mot_Enc2 = DC Motor with two-phase hall-encoder [part_number=VT-E-G25A-06-177E]
  JP1 = FTDI_BASIC [package=ftdi_basic]
  JP2 = FTDI_BASIC [package=ftdi_basic]
  JP3 = FTDI_BASIC [package=ftdi_basic]
  JP4 = FTDI_BASIC [package=ftdi_basic]

nets:
  N1: Mod1.pin_1, Bauteil1.STBY, Bauteil2.STBY
  N2: Mod1.pin_4, Bauteil1.PWMA
  N3: Mod1.pin_5, Bauteil1.PWMB
  N4: Mod1.pin_6, Bauteil2.PWMA
  N5: Mod1.pin_7, Bauteil2.PWMB
  N6: Mod1.pin_9, DC_Mot_Enc4.pin3
  N7: Mod1.pin_10, DC_Mot_Enc4.pin4
  N8: Mod1.pin_11, DC_Mot_Enc1.pin3
  N9: Mod1.pin_12, DC_Mot_Enc1.pin4
  N10: Mod1.pin_14, DC_Mot_Enc2.pin4
  N11: Mod1.pin_15, DC_Mot_Enc2.pin3
  N12: Mod1.pin_16, DC_Mot_Enc3.pin3
  N13: Mod1.pin_17, DC_Mot_Enc3.pin4
  N14: Mod1.pin_22, Bauteil1.BIN2
  N15: Mod1.pin_24, Bauteil1.AIN2
  N16: Mod1.pin_25, Bauteil1.AIN1
  N17: Mod1.pin_26, Bauteil1.BIN1
  N18: Mod1.pin_27, Bauteil2.AIN1
  N19: Mod1.pin_29, Bauteil2.AIN2
  N20: Mod1.pin_31, Bauteil2.BIN2
  N21: Mod1.pin_32, Bauteil2.BIN1
  GND 3V3/GND12V: Bauteil1.GND, Bauteil2.GND, DC_Mot_Enc1.pin5, BAT1.negative, DC_Mot_Enc3.pin5, DC_Mot_Enc4.pin5, DC_Mot_Enc2.pin5, JP2.5, JP2.1, JP2.6, JP2.2, JP2.3, JP2.4, JP3.5, JP3.1, JP3.6, JP3.2, JP3.3, JP3.4
  N22: Bauteil1.B01, DC_Mot_Enc3.pin1
  N23: Bauteil1.B02, DC_Mot_Enc3.pin6
  N24: Bauteil1.A02, DC_Mot_Enc1.pin6
  N25: Bauteil1.A01, DC_Mot_Enc1.pin1
  12V/3V3: Bauteil1.VCC, Bauteil2.VCC, DC_Mot_Enc1.pin2, BAT1.positive, DC_Mot_Enc3.pin2, DC_Mot_Enc4.pin2, DC_Mot_Enc2.pin2, JP1.5, JP1.1, JP1.6, JP1.2, JP1.3, JP1.4, JP4.5, JP4.1, JP4.6, JP4.2, JP4.3, JP4.4
  N26: Bauteil2.B01, DC_Mot_Enc4.pin6
  N27: Bauteil2.B02, DC_Mot_Enc4.pin1
  N28: Bauteil2.A02, DC_Mot_Enc2.pin1
  N29: Bauteil2.A01, DC_Mot_Enc2.pin6

notes:
  BLDC
  ESC

custom parts:
  Raspberry Pi Pico: Raspberry Pi Pico. Based around the RP2040 microcontroller the Pico is a low cost microcontroller device bringing Raspberry Pi quality, cost, and easy of use to the microcontroller space. Jan 2021, Split part in to two versions: tht (this one) and SMD. This one will drill holes for a .1 in header in pcb to allow plugging in the module as well as providing pads to solder the module to the top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
